// Logisim project proj_2_1_top.circ as structural Verilog
module TOP (
  input  clk,
  input  rst,
  input  [31:0] inst,
  output [31:0] inst_addr,
  output mem_wen,
  output [31:0] mem_din,
  output [31:0] mem_dout,
  output [31:0] mem_addr,
  output control_en,
  output [31:0] control_pc,
  output wb_en,
  output [4:0] wb_addr,
  output [31:0] wb_data
);

  wire comparator_2_eq, comparator_3_eq, comparator_4_eq, U, wb_src;
  wire [31:0] alu_result, multiplexer_1_out, multiplexer_2_out, next_inst_addr, rs1_data, rs2_data;

  Register #(.width(32)) PC (.D(next_inst_addr), .clk(clk), .Q(inst_addr), .clr(rst));  // open: en
  Multiplexer #(.width(32)) multiplexer_1 (.in0(mem_dout), .in1(alu_result), .out(multiplexer_1_out), .sel(wb_src));
  Comparator #(.mode("unsigned"), .width(5)) comparator_1 (.a(inst[4:0]), .b(5'b10111), .eq(U));  // open: gt, lt
  Multiplexer #(.width(32)) multiplexer_2 (.in0(32'h4), .in1(control_pc), .out(multiplexer_2_out), .sel(control_en));
  Multiplexer #(.width(32)) multiplexer_3 (
    .in0(multiplexer_1_out), .in1({inst[31:12], {12{1'b0}}}), .out(wb_data), .sel(U));
  Adder #(.width(32)) adder_1 (.a(multiplexer_2_out), .b(inst_addr), .out(next_inst_addr));  // open: cin, cout
  Comparator #(.mode("unsigned"), .width(6)) comparator_2 (
    .a(inst[5:0]), .b(6'b100011), .eq(comparator_2_eq));  // open: gt, lt
  Comparator #(.mode("unsigned"), .width(7)) comparator_3 (
    .a(inst[6:0]), .b(7'b1100011), .eq(comparator_3_eq));  // open: gt, lt
  Comparator #(.mode("unsigned"), .width(7)) comparator_4 (
    .a(inst[6:0]), .b(7'b1101111), .eq(comparator_4_eq));  // open: gt, lt
  not not_1 (wb_en, comparator_2_eq);
  or or_1 (control_en, comparator_3_eq, comparator_4_eq);
  regfile regfile_1 (
    .clk(clk), .rs1(inst[19:15]), .rs2(inst[24:20]), .wb_en(wb_en), .wb_addr(inst[11:7]), .wb_data(wb_data),
    .rs1_data(rs1_data), .rs2_data(rs2_data));

  assign wb_addr = inst[11:7];

  // Other names for the same wires on the sheet: opcode[6:0] = inst[6:0]; func3[2:0] = inst[14:12];
  //   U_imm[31:12] = inst[31:12]; rs1[4:0] = inst[19:15]; rs2[4:0] = inst[24:20]; func7[6:0] = inst[31:25]

  // Notes on the sheet:
  //   PC
  //   WB
  //   U-type
  //   DON'T TOUCH!
  //   regfile
  //   J/B-type
endmodule

module testbench (
  input  rst,
  output [5:0] out_2,
  output out_3,
  output halt,
  output [31:0] out_5,
  output [31:0] mem_dout,
  output [31:0] mem_addr,
  output out_8,
  output [31:0] out_9,
  output out_10,
  output [4:0] out_11,
  output [31:0] out_12
);

  wire and_1_out, carry, clk, not_1_out, not_2_out, por_1_out, rst_t;
  wire [31:0] inst, inst_addr;

  not not_1 (not_1_out, inst[2]);
  not not_2 (not_2_out, inst[3]);
  POR por_1 (.out(por_1_out));
  TOP top_1 (
    .clk(clk), .rst(rst_t), .inst(inst), .inst_addr(inst_addr), .mem_wen(out_3), .mem_din(out_5),
    .mem_dout(mem_dout), .mem_addr(mem_addr), .control_en(out_8), .control_pc(out_9), .wb_en(out_10),
    .wb_addr(out_11), .wb_data(out_12));
  Clock clock_1 (.out(clk));
  or or_1 (rst_t, rst, por_1_out);
  and and_1 (and_1_out, inst[0], inst[1], not_1_out, not_2_out, inst[4], inst[5], inst[6]);
  or or_2 (halt, and_1_out, carry);
  Counter #(.max('h3f), .width(6)) counter_1 (
    .clr(rst_t), .up(1'b1), .count(1'b1), .clk(clk), .carry(carry), .Q(out_2));  // open: load, D
  // ROM #(.line("quad"), .misaligned("true")) inst_mem: pin names not known; wires that end beside it: inst_addr[7:0], inst[7:0], inst[15:8], inst[23:16], inst[31:24]
  // Probe on inst

  // Other names for the same wires on the sheet: control_en = out_8; control_pc[31:0] = out_9; mem_din[31:0] = out_5;
  //   mem_wen = out_3; wb_addr[4:0] = out_11; wb_data[31:0] = out_12; wb_en = out_10

  // Notes on the sheet:
  //   DON'T TOUCH!
  //   contents of inst_mem (hex, n*v repeats v):
  //   b7 50 2 0 b3 80 20 0 0 10 11 23 0 10 21 3 0 21 1 63 51 b7
  //   you can write any instruction in
endmodule

module regfile (
  input  clk,
  input  [4:0] rs1,
  input  [4:0] rs2,
  input  wb_en,
  input  [4:0] wb_addr,
  input  [31:0] wb_data,
  output [31:0] rs1_data,
  output [31:0] rs2_data
);

  wire rst;
  wire [3:0] demultiplexer_1_out0, demultiplexer_1_out4, demultiplexer_1_out8, demultiplexer_1_out12,
       demultiplexer_1_out16, demultiplexer_1_out20, demultiplexer_1_out24, demultiplexer_1_out28;
  wire [31:0] x0_q, x1_q, x2_q, x3_q, x4_q, x5_q, x6_q, x7_q, x8_q, x9_q, x10_q, x11_q, x12_q, x13_q, x14_q,
       x15_q, x16_q, x17_q, x18_q, x19_q, x20_q, x21_q, x22_q, x23_q, x24_q, x25_q, x26_q, x27_q, x28_q,
       x29_q, x30_q, x31_q;

  Demultiplexer #(.select(5)) demultiplexer_1 (
    .out0(demultiplexer_1_out0[0]), .out1(demultiplexer_1_out0[1]), .out2(demultiplexer_1_out0[2]),
    .out3(demultiplexer_1_out0[3]), .out4(demultiplexer_1_out4[0]), .out5(demultiplexer_1_out4[1]),
    .out6(demultiplexer_1_out4[2]), .out7(demultiplexer_1_out4[3]), .out8(demultiplexer_1_out8[0]),
    .out9(demultiplexer_1_out8[1]), .out10(demultiplexer_1_out8[2]), .out11(demultiplexer_1_out8[3]),
    .out12(demultiplexer_1_out12[0]), .out13(demultiplexer_1_out12[1]), .out14(demultiplexer_1_out12[2]),
    .out15(demultiplexer_1_out12[3]), .out16(demultiplexer_1_out16[0]), .out17(demultiplexer_1_out16[1]),
    .out18(demultiplexer_1_out16[2]), .out19(demultiplexer_1_out16[3]), .out20(demultiplexer_1_out20[0]),
    .out21(demultiplexer_1_out20[1]), .out22(demultiplexer_1_out20[2]), .out23(demultiplexer_1_out20[3]),
    .out24(demultiplexer_1_out24[0]), .out25(demultiplexer_1_out24[1]), .out26(demultiplexer_1_out24[2]),
    .out27(demultiplexer_1_out24[3]), .out28(demultiplexer_1_out28[0]), .out29(demultiplexer_1_out28[1]),
    .out30(demultiplexer_1_out28[2]), .out31(demultiplexer_1_out28[3]), .in(wb_en), .sel(wb_addr));
  Register #(.width(32)) x0 (.D(wb_data), .en(1'b0), .clk(clk), .Q(x0_q), .clr(rst));
  Register #(.width(32)) x4 (.D(wb_data), .en(demultiplexer_1_out4[0]), .clk(clk), .Q(x4_q), .clr(rst));
  Register #(.width(32)) x8 (.D(wb_data), .en(demultiplexer_1_out8[0]), .clk(clk), .Q(x8_q), .clr(rst));
  Register #(.width(32)) x12 (.D(wb_data), .en(demultiplexer_1_out12[0]), .clk(clk), .Q(x12_q), .clr(rst));
  Register #(.width(32)) x16 (.D(wb_data), .en(demultiplexer_1_out16[0]), .clk(clk), .Q(x16_q), .clr(rst));
  Register #(.width(32)) x20 (.D(wb_data), .en(demultiplexer_1_out20[0]), .clk(clk), .Q(x20_q), .clr(rst));
  Register #(.width(32)) x24 (.D(wb_data), .en(demultiplexer_1_out24[0]), .clk(clk), .Q(x24_q), .clr(rst));
  Register #(.width(32)) x28 (.D(wb_data), .en(demultiplexer_1_out28[0]), .clk(clk), .Q(x28_q), .clr(rst));
  Register #(.width(32)) x1 (.D(wb_data), .en(demultiplexer_1_out0[1]), .clk(clk), .Q(x1_q), .clr(rst));
  Register #(.width(32)) x5 (.D(wb_data), .en(demultiplexer_1_out4[1]), .clk(clk), .Q(x5_q), .clr(rst));
  Register #(.width(32)) x9 (.D(wb_data), .en(demultiplexer_1_out8[1]), .clk(clk), .Q(x9_q), .clr(rst));
  Register #(.width(32)) x13 (.D(wb_data), .en(demultiplexer_1_out12[1]), .clk(clk), .Q(x13_q), .clr(rst));
  Register #(.width(32)) x17 (.D(wb_data), .en(demultiplexer_1_out16[1]), .clk(clk), .Q(x17_q), .clr(rst));
  Register #(.width(32)) x21 (.D(wb_data), .en(demultiplexer_1_out20[1]), .clk(clk), .Q(x21_q), .clr(rst));
  Register #(.width(32)) x25 (.D(wb_data), .en(demultiplexer_1_out24[1]), .clk(clk), .Q(x25_q), .clr(rst));
  Register #(.width(32)) x29 (.D(wb_data), .en(demultiplexer_1_out28[1]), .clk(clk), .Q(x29_q), .clr(rst));
  Register #(.width(32)) x2 (.D(wb_data), .en(demultiplexer_1_out0[2]), .clk(clk), .Q(x2_q), .clr(rst));
  Register #(.width(32)) x6 (.D(wb_data), .en(demultiplexer_1_out4[2]), .clk(clk), .Q(x6_q), .clr(rst));
  Register #(.width(32)) x10 (.D(wb_data), .en(demultiplexer_1_out8[2]), .clk(clk), .Q(x10_q), .clr(rst));
  Register #(.width(32)) x14 (.D(wb_data), .en(demultiplexer_1_out12[2]), .clk(clk), .Q(x14_q), .clr(rst));
  Register #(.width(32)) x18 (.D(wb_data), .en(demultiplexer_1_out16[2]), .clk(clk), .Q(x18_q), .clr(rst));
  Register #(.width(32)) x22 (.D(wb_data), .en(demultiplexer_1_out20[2]), .clk(clk), .Q(x22_q), .clr(rst));
  Register #(.width(32)) x26 (.D(wb_data), .en(demultiplexer_1_out24[2]), .clk(clk), .Q(x26_q), .clr(rst));
  Register #(.width(32)) x30 (.D(wb_data), .en(demultiplexer_1_out28[2]), .clk(clk), .Q(x30_q), .clr(rst));
  Register #(.width(32)) x3 (.D(wb_data), .en(demultiplexer_1_out0[3]), .clk(clk), .Q(x3_q), .clr(rst));
  Register #(.width(32)) x7 (.D(wb_data), .en(demultiplexer_1_out4[3]), .clk(clk), .Q(x7_q), .clr(rst));
  Register #(.width(32)) x11 (.D(wb_data), .en(demultiplexer_1_out8[3]), .clk(clk), .Q(x11_q), .clr(rst));
  Register #(.width(32)) x15 (.D(wb_data), .en(demultiplexer_1_out12[3]), .clk(clk), .Q(x15_q), .clr(rst));
  Register #(.width(32)) x19 (.D(wb_data), .en(demultiplexer_1_out16[3]), .clk(clk), .Q(x19_q), .clr(rst));
  Register #(.width(32)) x23 (.D(wb_data), .en(demultiplexer_1_out20[3]), .clk(clk), .Q(x23_q), .clr(rst));
  Register #(.width(32)) x27 (.D(wb_data), .en(demultiplexer_1_out24[3]), .clk(clk), .Q(x27_q), .clr(rst));
  Register #(.width(32)) x31 (.D(wb_data), .en(demultiplexer_1_out28[3]), .clk(clk), .Q(x31_q), .clr(rst));
  Multiplexer #(.select(5), .width(32)) multiplexer_1 (
    .in0(x0_q), .in1(x1_q), .in2(x2_q), .in3(x3_q), .in4(x4_q), .in5(x5_q), .in6(x6_q), .in7(x7_q),
    .in8(x8_q), .in9(x9_q), .in10(x10_q), .in11(x11_q), .in12(x12_q), .in13(x13_q), .in14(x14_q),
    .in15(x15_q), .in16(x16_q), .in17(x17_q), .in18(x18_q), .in19(x19_q), .in20(x20_q), .in21(x21_q),
    .in22(x22_q), .in23(x23_q), .in24(x24_q), .in25(x25_q), .in26(x26_q), .in27(x27_q), .in28(x28_q),
    .in29(x29_q), .in30(x30_q), .in31(x31_q), .out(rs1_data), .sel(rs1));
  Multiplexer #(.select(5), .width(32)) multiplexer_2 (
    .in0(x0_q), .in1(x1_q), .in2(x2_q), .in3(x3_q), .in4(x4_q), .in5(x5_q), .in6(x6_q), .in7(x7_q),
    .in8(x8_q), .in9(x9_q), .in10(x10_q), .in11(x11_q), .in12(x12_q), .in13(x13_q), .in14(x14_q),
    .in15(x15_q), .in16(x16_q), .in17(x17_q), .in18(x18_q), .in19(x19_q), .in20(x20_q), .in21(x21_q),
    .in22(x22_q), .in23(x23_q), .in24(x24_q), .in25(x25_q), .in26(x26_q), .in27(x27_q), .in28(x28_q),
    .in29(x29_q), .in30(x30_q), .in31(x31_q), .out(rs2_data), .sel(rs2));
endmodule

module imm_gen (
  input  [31:0] inst
);
endmodule
